# Fritzing sketch just a Dehumidifer (saved by Fritzing 0.9.4)

parts:
  PC_FAN = DC Motor
  Peltier = Peltier Element
  +12_DC_Male = Power Jack [package=power_jack_slot]
  U1 = Module 4 Relais 5V [package="Module 4 Relais 5V"]
  MP1584EN = Mini-360 DC-DC Buck converter [package=THT]
  USB_Micro_Male = USB_MICROB_PLUG [package=micro-b-ra-th]

nets:
  N1: PC_FAN.pin_1, Peltier.pin1, +12_DC_Male.GND, MP1584EN.IN-
  N2: PC_FAN.pin_2, U1.K2-NO
  N3: Peltier.pin2, U1.K1-NO
  N4: +12_DC_Male.PWR, U1.K1-NF, U1.K2-NF, MP1584EN.IN+
  N5: MP1584EN.OUT+, USB_Micro_Male.VCC
  N6: MP1584EN.OUT-, USB_Micro_Male.GND

notes:
  Set to 5V
  To Grove
  D7 and D8
  To Grove USB
  JustBarran/youtube

custom parts:
  Module 4 Relais 5V: Module 4 Relais 5V 4x SPD-06VDC-SD-C
  Mini-360 DC-DC Buck converter: Mini-360 DC-DC Buck converter. Tiny buck step down voltage converter, input voltage 4.75 to 23V output 1 to 17V adjustable. Available from ebay and the like.
