# Fritzing sketch musical_layout_recover (saved by Fritzing 0.9.4)

parts:
  C1 = Ceramic Capacitor [capacitance=100nF part_number=104 package="100 mil [THT, multilayer]"]  # not connected
  C2 = Ceramic Capacitor [capacitance=0.1nF part_number=103 package="100 mil [THT, multilayer]"]  # not connected
  R1 = Resistor [tolerance=±5% resistance=22k package=THT]
  R2 = Resistor [tolerance=±5% resistance=22k package=THT]
  C3 = Ceramic Capacitor [capacitance=100nF part_number=104 package="100 mil [THT, multilayer]"]
  R3 = Resistor [tolerance=±5% resistance=220k part_number=200k package=THT]  # not connected
  C4 = Ceramic Capacitor [capacitance=10nF part_number=33 package="100 mil [THT, multilayer]"]
  Arduino_Mini = Arduino Mini (Rev5)
  8x8_LED_Modul_mit_MAX1 = 8x8 LED Modul mit MAX7219 [package=THT]
  J1 = Dagu DGServo 9g header (male) [package=THT]
  J2 = Dagu DGServo 9g header (male) [package=THT]
  J3 = Dagu DGServo 9g header (male) [package=THT]
  J4 = Dagu DGServo 9g header (male) [package=THT]
  R4 = TRIMPOT [package=3386u]
  J5 = Power Jack [package=power_jack_slot]
  U1 = 2.5mm Audio Jack [package=stereojack2.5mm_stereojack2.5mm]
  U2 = 2.5mm Audio Jack [package=stereojack2.5mm_stereojack2.5mm]
  R5 = Resistor [tolerance=±5% resistance=22k package=THT]
  Mini_MP1584EN = Mini-360 DC-DC Buck converter [package=THT]

nets:
  N1: R1.Pin_0, R2.Pin_0, C4.1
  N2: R1.Pin_1, U1.RIGHT, U2.RIGHT
  N3: R2.Pin_1, U1.LEFT, U2.LEFT
  N4: C3.1, R5.Pin_0
  GND: Arduino_Mini.GND, 8x8_LED_Modul_mit_MAX1.GND_Eingang, J1.gnd, J3.gnd, R4.CW, Mini_MP1584EN.OUT-
  N5: Arduino_Mini.D2, J1.Vcc
  N6: Arduino_Mini.D3_PWM, J1.pulse
  N7: Arduino_Mini.D4, J2.gnd
  N8: Arduino_Mini.D5_PWM, J2.Vcc
  N9: Arduino_Mini.D6_PWM, J3.Vcc
  N10: Arduino_Mini.D7, J3.pulse
  N11: Arduino_Mini.D8, J4.gnd
  N12: Arduino_Mini.5V, 8x8_LED_Modul_mit_MAX1.VCC_Eingang, J2.pulse, J4.pulse, R4.CCW, Mini_MP1584EN.OUT+
  N13: Arduino_Mini.A1, R4.WIPER
  N14: Arduino_Mini.D12, 8x8_LED_Modul_mit_MAX1.CLK_Eingang
  N15: Arduino_Mini.D11_PWM, 8x8_LED_Modul_mit_MAX1.CS_Eingang
  N16: Arduino_Mini.D10_PWM, 8x8_LED_Modul_mit_MAX1.DIN_Eingang
  N17: J5.GND, Mini_MP1584EN.IN-
  N18: J5.PWR, Mini_MP1584EN.IN+
  N19: U1.SLEEVE, U2.SLEEVE, R5.Pin_1

notes:
  2.54 header to Relay Board2 These would be a JST Male
  2.54 header to Relay Board 1 These would be a JST Male
  Audio Jacks 3.5mm
  DC barrel jack
  5.5mmx 2.1mm

custom parts:
  Mini-360 DC-DC Buck converter: Mini-360 DC-DC Buck converter. Tiny buck step down voltage converter, input voltage 4.75 to 23V output 1 to 17V adjustable. Available from ebay and the like.
